# Fritzing sketch schematic (saved by Fritzing 0.9.4)

parts:
  U1 = LIPO-110mAh [package=lipo-110]
  U2 = LIPO-110mAh [package=lipo-110]
  Mod1 = 2S-BMS
  C1 = Capacitor Polarized [part_number="470 micro" package=panasonic_h13]
  C2 = Ceramic Capacitor [capacitance=100nF package="200 mil [THT, multilayer]"]  # not connected
  DC1 = DC_DC_XL4016 [package=board_screw]
  Part1 = Motor Driver 1A Dual TB6612FNG
  C3 = Capacitor Polarized [part_number="470 micro" package=panasonic_h13]  # not connected
  C4 = Ceramic Capacitor [capacitance=100nF package="200 mil [THT, multilayer]"]
  U3 = ESP32-38PinWide [part_number=ESP32-38PinWide]
  M1 = DC Motor
  M2 = DC Motor

nets:
  N1: U1.+, Mod1.pin3#4
  N2: U1.-, Mod1.pin2
  N3: U2.+, Mod1.pin1
  N4: Mod1.pin3#3, C1.+
  N5: DC1.IN+, Part1.VM
  N6: DC1.OUT+, C4.1, U3.VIN
  N7: DC1.OUT-, C4.0, U3.GPIO11
  GND: Part1.GND, U3.GND
  N8: Part1.B01, M2.pin_2
  N9: Part1.B02, M2.pin_1
  N10: Part1.A02, M1.pin_2
  N11: Part1.A01, M1.pin_1
  N12: Part1.VCC, U3.3.3
  N13: Part1.PWMA, U3.GPIO6
  N14: Part1.AIN2, U3.GPIO5
  N15: Part1.AIN1, U3.GPIO4
  N16: Part1.STBY, U3.GPIO17
  N17: Part1.BIN1, U3.GPIO7
  N18: Part1.BIN2, U3.GPIO15

custom parts:
  2S-BMS: 2S-BMS LIPO battery charger / protection unit. Note pcb does not match the board as it will likely connect with wires, so pcb is 5 pads suitable for .1in header pins.
  ESP32-38PinWide: Generic 38-Pin ESP32 with wide format (only access to one side of pins on a breadboard) based on Stephen Lilley's HiLetgo ESP-WROOM-32 ESP32 ESP-32S Development Board.
